# Fritzing sketch esp8266 (saved by Fritzing 0.8.7b)
breadboards: 1

parts:
  Part1 = Arduino Nano (Rev3.0)
  U1 = ESP8266 WiFi Module [part_number=ESP8266]

nets:
  N1: Part1.D1/TX, U1.TXD
  N2: Part1.D0/RX, U1.RXD
  GND: Part1.GND, U1.GND
  N3: Part1.3V3, U1.CH_PD

custom parts:
  ESP8266 WiFi Module: Generic WiFi Module based on the ESP8266 with onboard PCB antenna and UART communications
