# Fritzing sketch hc-sr04 (saved by Fritzing 0.8.7b)
breadboards: 1

parts:
  Part1 = Arduino Nano (Rev3.0)
  Part2 = SRF05 Ultrasonic Rangefinder
  R1 = Resistor [tolerance=±5% resistance=220 package=THT]
  R2 = Resistor [tolerance=±5% resistance=220 package=THT]
  VCC1 = Battery
  R3 = Resistor [tolerance=±5% resistance=220 package=THT]
  R4 = Resistor [tolerance=±5% resistance=220 package=THT]

nets:
  GND: Part1.GND, Part2.Echo, Part2.GND, R1.Pin_0, VCC1.-, R3.Pin_1
  N1: Part1.D2, Part2.Trig
  N2: Part1.D3, R3.Pin_0, R4.Pin_1
  N3: Part2.VCC, R1.Pin_1, R2.Pin_1
  N4: R2.Pin_0, VCC1.+

notes:
  1K Ohm
  200 Ohm
  2K Ohm
  6V
